# Fritzing sketch aaron_barlow_personal_project (saved by Fritzing 0.9.3b)
breadboards: 1

parts:
  Part1 = Arduino Ethernet Shield (Rev3)
  Part2 = Adafruit 1.44 inch TFT Breakout [part_number="Adafruit #2088"]
  R1 = Trimmer Potentiometer [maximum_resistance=10kΩ package=THT]
  R2 = Trimmer Potentiometer [maximum_resistance=10kΩ package=THT]
  S1 = Momentary Switch [package=ksa_sealed_tac_switch]
  R3 = Resistor [tolerance=±5% resistance=10k package=THT]
  LED1 = LED - 5mm [color="Red (633nm)" package="5 mm [THT]"]
  R4 = Resistor [tolerance=±5% resistance=220 package=THT]

nets:
  N1: Part1.D8, Part2.TFTDC
  N2: Part1.PWM_D9, Part2.RESET
  N3: Part1.ETH_CS, Part2.TFTCS
  N4: Part1.PWM_D11, Part2.MOSI
  N5: Part1.SPI/D13, Part2.SCK
  N6: Part1.A0, R1.wiper
  N7: Part1.A1, R2.wiper
  N8: Part1.SDCS, S1.1
  N9: Part1.PWM_D6, R4.Pin_1
  GND: Part1.GND, Part2.GND, R1.leg1, R2.leg1, LED1.cathode
  VIN: Part1.VIN, Part2.VIN, R1.leg2, R2.leg2, R3.Pin_1
  N10: S1.3, R3.Pin_0
  N11: LED1.anode, R4.Pin_0

custom parts:
  Adafruit 1.44 inch TFT Breakout: This lovely little display breakout is the best way to add a small, colorful and bright display to any project. Since the display uses 4-wire SPI to communicate and has its own pixel-addressable frame buffer, it can be used with every kind of microcontroller. Even a very small one with low memory and few pins available! The 1.44" display has 128x128 color pixels. Unlike the low cost "Nokia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
